// Logisim project CPU.circ as structural Verilog: 8 circuits, main circuit ALU
// ALU
module main (
);

  wire alu_1_carry_out, bitfinder_1_found, Carry_q, comparator_1_eq, control_unit_1_p3, control_unit_1_p4,
       control_unit_1_p5, control_unit_1_p6, undriven_4, undriven_6, undriven_7, undriven_8, undriven_9,
       undriven_11, undriven_12;
  wire [1:0] control_unit_1_p1, undriven_5;
  wire [3:0] Extender_out_2, Extender_out_2_2, Extender_out_2_3, Extender_out_2_4, multiplexer_2_out,
       multiplexer_2_out_3, multiplexer_4_out, spliter_nibble, undriven_10;
  wire [7:4] multiplexer_2_out_2;
  wire [11:0] multiplexer_1_out, PC_q, undriven, undriven_2, undriven_3;
  wire [15:0] bit_extender_1_out, controlled_buffer_1_out, Data_Register_q, extender_2_out_2,
       Extender_3_out_2, multiplexer_3_out, multiplexer_5_out, multiplexer_6_out, spliter_full_output;

  Multiplexer #(.select(2), .width(12), .enable("false")) multiplexer_1 (
    .in0(undriven_3), .in1(undriven), .in2(undriven_2), .out(multiplexer_1_out), .sel(control_unit_1_p1));  // open: in3
  extender Extender (.in_1(undriven_2), .out_2({Extender_out_2_4, Extender_out_2_3, Extender_out_2_2, Extender_out_2}));
  Hex_Digit_Display hex_digit_display_1 (.value(multiplexer_2_out_3));  // open: dp
  extender extender_2 (.in_1(undriven), .out_2(extender_2_out_2));
  extender Extender_3 (.in_1(undriven_3), .out_2(Extender_3_out_2));
  Register #(.width(12)) PC (.D(multiplexer_1_out), .en(1'b1), .Q(PC_q), .clk(control_unit_1_p3));  // open: clr
  Hex_Digit_Display hex_digit_display_2 (.value(multiplexer_2_out));  // open: dp
  Hex_Digit_Display hex_digit_display_3 (.value(multiplexer_2_out_2));  // open: dp
  Multiplexer #(.width(12), .enable("false")) multiplexer_2 (
    .in0(undriven), .in1(PC_q), .out({multiplexer_2_out_3, multiplexer_2_out_2, multiplexer_2_out}),
    .sel(control_unit_1_p4));
  Hex_Digit_Display hex_digit_display_4 (.value(Extender_out_2_4));  // open: dp
  Hex_Digit_Display hex_digit_display_5 (.value(Extender_out_2_3));  // open: dp
  assign bit_extender_1_out = {{4{1'b0}}, PC_q};  // Bit_Extender bit_extender_1
  Hex_Digit_Display hex_digit_display_6 (.value(Extender_out_2));  // open: dp
  Hex_Digit_Display hex_digit_display_7 (.value(Extender_out_2_2));  // open: dp
  RAM #(.addrWidth(12), .dataWidth(16)) ram_1 (
    .addr({multiplexer_2_out_3, multiplexer_2_out_2, multiplexer_2_out}),
    .data({Extender_out_2_4, Extender_out_2_3, Extender_out_2_2, Extender_out_2}), .sel(1'b1),
    .clk(control_unit_1_p5), .ld(control_unit_1_p6));  // open: clr
  // Control__Unit control_unit_1: pin names not known; wires that end beside it: control_unit_1_p1[0], control_unit_1_p1[1], control_unit_1_p3, control_unit_1_p4, control_unit_1_p5, control_unit_1_p6
  assign controlled_buffer_1_out = control_unit_1_p6 ? {Extender_out_2_4, Extender_out_2_3, Extender_out_2_2, Extender_out_2} : 16'bz;  // Controlled_Buffer controlled_buffer_1
  Register #(.width(16)) IR (
    .D(controlled_buffer_1_out), .en(1'b1), .Q(Extender_3_out_2), .clk(undriven_4));  // open: clr
  split_nibble spliter (.\input (Extender_3_out_2), .nibble(spliter_nibble), .full_output(spliter_full_output));
  Register #(.width(16)) Data_Register (
    .D({Extender_out_2_4, Extender_out_2_3, Extender_out_2_2, Extender_out_2}), .en(1'b1),
    .Q(Data_Register_q), .clk(undriven_7));  // open: clr
  Hex_Digit_Display hex_digit_display_8 (.value(undriven_10));  // open: dp
  Multiplexer #(.select(2), .width(16), .enable("false")) multiplexer_3 (
    .in0(extender_2_out_2), .in1(spliter_full_output),
    .in2({Extender_out_2_4, Extender_out_2_3, Extender_out_2_2, Extender_out_2}), .out(multiplexer_3_out),
    .sel(undriven_5));  // open: in3
  Multiplexer #(.width(4), .enable("false")) multiplexer_4 (
    .in0(spliter_nibble), .in1(4'b0000), .out(multiplexer_4_out), .sel(undriven_9));
  Register #(.width(16)) Accumulator (
    .D(multiplexer_3_out), .en(1'b1),
    .Q({Extender_out_2_4, Extender_out_2_3, Extender_out_2_2, Extender_out_2}), .clk(undriven_6));  // open: clr
  Multiplexer #(.width(16), .enable("false")) multiplexer_5 (
    .in0(Data_Register_q), .in1({16{1'b1}}), .out(multiplexer_5_out), .sel(undriven_11));
  Multiplexer #(.width(16), .enable("false")) multiplexer_6 (
    .in0({Extender_out_2_4, Extender_out_2_3, Extender_out_2_2, Extender_out_2}), .in1(bit_extender_1_out),
    .out(multiplexer_6_out), .sel(undriven_8));
  BitFinder #(.width(16), .\type ("high1")) bitfinder_1 (
    .in({Extender_out_2_4, Extender_out_2_3, Extender_out_2_2, Extender_out_2}), .found(bitfinder_1_found));  // open: index
  ALU alu_1 (
    .carry_in(Carry_q), .input_A(multiplexer_6_out), .input_B(multiplexer_5_out),
    .\output (extender_2_out_2), .Carry_out(alu_1_carry_out), .opcode(multiplexer_4_out));  // open: enable
  Register #(.width(1)) Carry (.D(alu_1_carry_out), .en(1'b1), .Q(Carry_q), .clk(undriven_12));  // open: clr
  Comparator #(.width(16)) comparator_1 (
    .a({Extender_out_2_4, Extender_out_2_3, Extender_out_2_2, Extender_out_2}), .b({16{1'b0}}),
    .eq(comparator_1_eq));  // open: gt, lt
endmodule

module ALU (
  input  carry_in,
  input  [15:0] input_A,
  input  [15:0] input_B,
  input  [3:0] opcode,
  input  enable,
  output [15:0] \output ,
  output Carry_out
);

  wire [2:0] bit_extender_1_out;
  wire [15:0] adder_1_out, and_1_out, demultiplexer_1_out0, demultiplexer_1_out2, demultiplexer_1_out4,
       demultiplexer_1_out5, demultiplexer_1_out6, demultiplexer_1_out7, demultiplexer_2_out0,
       demultiplexer_2_out2, demultiplexer_2_out4, demultiplexer_2_out5, demultiplexer_2_out6, not_1_out,
       or_1_out, subtractor_1_out, xor_1_out;

  Bit_Extender #(.in_width(4), .out_width(3)) bit_extender_1 (.in(opcode), .out(bit_extender_1_out));
  Demultiplexer #(.select(3), .width(16)) demultiplexer_1 (
    .out0(demultiplexer_1_out0), .out2(demultiplexer_1_out2), .out4(demultiplexer_1_out4),
    .out5(demultiplexer_1_out5), .out6(demultiplexer_1_out6), .out7(demultiplexer_1_out7), .in(input_A),
    .sel(bit_extender_1_out), .en(enable));  // open: out1, out3
  Demultiplexer #(.select(3), .width(16)) demultiplexer_2 (
    .out0(demultiplexer_2_out0), .out2(demultiplexer_2_out2), .out4(demultiplexer_2_out4),
    .out5(demultiplexer_2_out5), .out6(demultiplexer_2_out6), .in(input_B), .sel(bit_extender_1_out),
    .en(enable));  // open: out1, out3, out7
  Adder #(.width(16)) adder_1 (
    .a(demultiplexer_1_out0), .b(demultiplexer_2_out0), .out(adder_1_out), .cin(carry_in), .cout(Carry_out));
  Subtractor #(.width(16)) subtractor_1 (
    .a(demultiplexer_1_out2), .b(demultiplexer_2_out2), .out(subtractor_1_out), .bin(carry_in),
    .bout(Carry_out));
  assign and_1_out = demultiplexer_1_out4 & demultiplexer_2_out4;  // AND_Gate and_1, 16 bits wide
  assign or_1_out = demultiplexer_1_out5 | demultiplexer_2_out5;  // OR_Gate or_1, 16 bits wide
  assign xor_1_out = demultiplexer_1_out6 ^ demultiplexer_2_out6;  // XOR_Gate xor_1, 16 bits wide
  assign not_1_out = ~demultiplexer_1_out7;  // NOT_Gate not_1, 16 bits wide
  Multiplexer #(.select(3), .width(16)) multiplexer_1 (
    .in0(adder_1_out), .in2(subtractor_1_out), .in3(and_1_out), .in4(or_1_out), .in5(xor_1_out),
    .in6(not_1_out), .out(\output ), .sel(bit_extender_1_out), .en(enable));  // open: in1, in7
endmodule

// extend
module extender (
  input  [11:0] in_1,
  output [15:0] out_2
);


  assign out_2[11:0] = in_1;
endmodule

module split_nibble (
  input  [15:0] \input ,
  output [3:0] nibble,
  output [15:0] full_output
);


  assign full_output = {4'b0000, \input [11:0]};
  assign nibble = \input [15:12];
endmodule

module Control__Unit (
  input  [3:0] opcode,
  input  Z,
  input  M,
  input  C,
  output [3:0] state
);

  wire clock_1_out;
  wire [3:0] state_register_q;

  Clock clock_1 (.out(clock_1_out));
  CU_core cu_core_1 (
    .s3(state_register_q[3]), .s2(state_register_q[2]), .s1(state_register_q[1]), .s0(state_register_q[0]),
    .op3(opcode[3]), .op2(opcode[2]), .op1(opcode[1]), .op0(opcode[0]), .Z(Z), .M(M), .C(C), .NS3(state[3]),
    .NS2(state[2]), .NS1(state[1]), .NS0(state[0]));
  Register #(.width(4)) state_register (.D(state), .en(1'b1), .Q(state_register_q), .clk(clock_1_out));  // open: clr
endmodule

module CU_core (
  input  s3,
  input  s2,
  input  s1,
  input  s0,
  input  op3,
  input  op2,
  input  op1,
  input  op0,
  input  Z,
  input  M,
  input  C,
  output NS3,
  output NS2,
  output NS1,
  output NS0
);

  wire and_1_out, and_2_out, and_3_out, and_4_out, and_5_out, and_6_out, and_7_out, and_8_out, and_9_out,
       and_10_out, and_11_out, and_12_out, and_13_out, and_14_out, and_15_out, and_16_out, and_17_out,
       and_18_out, and_19_out, and_20_out, and_21_out, and_22_out, and_23_out, and_24_out, and_25_out,
       and_26_out, and_27_out, and_28_out, and_29_out, not_1_out, not_2_out, not_3_out, not_4_out, not_5_out,
       not_6_out, not_7_out, not_8_out, not_9_out, not_10_out, not_11_out, not_12_out, not_13_out,
       not_14_out, not_15_out, not_16_out, not_17_out, not_18_out, not_19_out, not_20_out, not_21_out,
       not_22_out, not_23_out, not_24_out, not_25_out, not_26_out, not_27_out, not_28_out, not_29_out,
       not_30_out, not_31_out, not_32_out, not_33_out, not_34_out, not_35_out, not_36_out, not_37_out,
       not_38_out, not_39_out, not_40_out, not_41_out, not_42_out, not_43_out, not_44_out, not_45_out,
       not_46_out, not_47_out, not_48_out, not_49_out, not_50_out, not_51_out, not_52_out, not_53_out,
       not_54_out, not_55_out, not_56_out, not_57_out, not_58_out, not_59_out, not_60_out, not_61_out,
       not_62_out, not_63_out, not_64_out, not_65_out, not_66_out, not_67_out, not_68_out, not_69_out,
       not_70_out, not_71_out, not_72_out, not_73_out, not_74_out, not_75_out, not_76_out, not_77_out,
       not_78_out, not_79_out, not_80_out, not_81_out, not_82_out, not_83_out, not_84_out, not_85_out,
       not_86_out, not_87_out, not_88_out, not_89_out, not_90_out, not_91_out, not_92_out, not_93_out,
       not_94_out, not_95_out, not_96_out, not_97_out, not_98_out, not_99_out, not_100_out, not_101_out,
       not_102_out, not_103_out, not_104_out, not_105_out, not_106_out, not_107_out, not_108_out,
       not_109_out, not_110_out, not_111_out, not_112_out, not_113_out, not_114_out, not_115_out,
       not_116_out, not_117_out, not_118_out, not_119_out, not_120_out, not_121_out, not_122_out,
       not_123_out, not_124_out, not_125_out;

  not not_1 (not_1_out, s3);
  not not_2 (not_2_out, s2);
  not not_3 (not_3_out, s1);
  not not_4 (not_4_out, op2);
  not not_5 (not_5_out, s3);
  not not_6 (not_6_out, s2);
  not not_7 (not_7_out, s1);
  not not_8 (not_8_out, op1);
  not not_9 (not_9_out, s3);
  not not_10 (not_10_out, s2);
  not not_11 (not_11_out, s1);
  not not_12 (not_12_out, op0);
  not not_13 (not_13_out, s3);
  not not_14 (not_14_out, s2);
  not not_15 (not_15_out, s1);
  not not_16 (not_16_out, s3);
  not not_17 (not_17_out, s2);
  not not_18 (not_18_out, s1);
  not not_19 (not_19_out, op1);
  not not_20 (not_20_out, op0);
  not not_21 (not_21_out, s3);
  not not_22 (not_22_out, op2);
  not not_23 (not_23_out, s3);
  not not_24 (not_24_out, s2);
  not not_25 (not_25_out, s1);
  not not_26 (not_26_out, op2);
  not not_27 (not_27_out, s3);
  not not_28 (not_28_out, s2);
  not not_29 (not_29_out, s0);
  not not_30 (not_30_out, op3);
  not not_31 (not_31_out, op1);
  not not_32 (not_32_out, s3);
  not not_33 (not_33_out, s2);
  not not_34 (not_34_out, s0);
  not not_35 (not_35_out, op3);
  not not_36 (not_36_out, op0);
  not not_37 (not_37_out, s3);
  not not_38 (not_38_out, s2);
  not not_39 (not_39_out, s1);
  not not_40 (not_40_out, op3);
  not not_41 (not_41_out, s3);
  not not_42 (not_42_out, s2);
  not not_43 (not_43_out, s1);
  not not_44 (not_44_out, op2);
  not not_45 (not_45_out, op1);
  not not_46 (not_46_out, s3);
  not not_47 (not_47_out, s2);
  not not_48 (not_48_out, s1);
  not not_49 (not_49_out, op2);
  not not_50 (not_50_out, op1);
  not not_51 (not_51_out, s3);
  not not_52 (not_52_out, s2);
  not not_53 (not_53_out, s1);
  not not_54 (not_54_out, op2);
  not not_55 (not_55_out, op0);
  not not_56 (not_56_out, s3);
  not not_57 (not_57_out, s2);
  not not_58 (not_58_out, s1);
  not not_59 (not_59_out, op3);
  not not_60 (not_60_out, op2);
  not not_61 (not_61_out, s3);
  not not_62 (not_62_out, s2);
  not not_63 (not_63_out, s1);
  not not_64 (not_64_out, op3);
  not not_65 (not_65_out, op1);
  not not_66 (not_66_out, s3);
  not not_67 (not_67_out, s2);
  not not_68 (not_68_out, s0);
  not not_69 (not_69_out, op3);
  not not_70 (not_70_out, op2);
  not not_71 (not_71_out, s3);
  not not_72 (not_72_out, s2);
  not not_73 (not_73_out, s1);
  not not_74 (not_74_out, op2);
  not not_75 (not_75_out, op1);
  not not_76 (not_76_out, s3);
  not not_77 (not_77_out, s2);
  not not_78 (not_78_out, s1);
  not not_79 (not_79_out, op2);
  not not_80 (not_80_out, op0);
  not not_81 (not_81_out, s3);
  not not_82 (not_82_out, s2);
  not not_83 (not_83_out, s1);
  not not_84 (not_84_out, op1);
  not not_85 (not_85_out, op0);
  not not_86 (not_86_out, s3);
  not not_87 (not_87_out, s2);
  not not_88 (not_88_out, s1);
  not not_89 (not_89_out, op3);
  not not_90 (not_90_out, op0);
  not not_91 (not_91_out, s3);
  not not_92 (not_92_out, s2);
  not not_93 (not_93_out, s1);
  not not_94 (not_94_out, op2);
  not not_95 (not_95_out, op1);
  not not_96 (not_96_out, op0);
  not not_97 (not_97_out, s3);
  not not_98 (not_98_out, s2);
  not not_99 (not_99_out, s1);
  not not_100 (not_100_out, op2);
  not not_101 (not_101_out, s3);
  not not_102 (not_102_out, s2);
  not not_103 (not_103_out, s1);
  not not_104 (not_104_out, op1);
  not not_105 (not_105_out, s3);
  not not_106 (not_106_out, s2);
  not not_107 (not_107_out, s1);
  not not_108 (not_108_out, op0);
  not not_109 (not_109_out, s3);
  not not_110 (not_110_out, s2);
  not not_111 (not_111_out, s1);
  not not_112 (not_112_out, s3);
  not not_113 (not_113_out, s2);
  not not_114 (not_114_out, s0);
  not not_115 (not_115_out, op3);
  not not_116 (not_116_out, op2);
  not not_117 (not_117_out, s3);
  not not_118 (not_118_out, s2);
  not not_119 (not_119_out, s1);
  not not_120 (not_120_out, op2);
  not not_121 (not_121_out, s3);
  not not_122 (not_122_out, s3);
  not not_123 (not_123_out, s2);
  not not_124 (not_124_out, s1);
  not not_125 (not_125_out, s0);
  and and_1 (and_1_out, not_121_out, s2, s1, s0);
  and and_2 (and_2_out, not_1_out, not_2_out, not_3_out, s0, op3, not_4_out, op1, op0);
  and and_3 (and_3_out, not_5_out, not_6_out, not_7_out, s0, op3, op2, not_8_out, op0, Z);
  and and_4 (and_4_out, not_9_out, not_10_out, not_11_out, s0, op3, op2, op1, not_12_out, M);
  and and_5 (and_5_out, not_13_out, not_14_out, not_15_out, s0, op3, op2, op1, op0, C);
  and and_6 (and_6_out, not_16_out, not_17_out, not_18_out, s0, op3, op2, not_19_out, not_20_out);
  and and_7 (and_7_out, not_21_out, s2, s1, s0, op3, not_22_out, op1, op0);
  and and_8 (and_8_out, not_23_out, not_24_out, not_25_out, s0, op3, not_26_out, op1, op0);
  and and_9 (and_9_out, not_27_out, not_28_out, s1, not_29_out, not_30_out, op2, not_31_out);
  and and_10 (and_10_out, not_32_out, not_33_out, s1, not_34_out, not_35_out, op2, op1, not_36_out);
  and and_11 (and_11_out, not_37_out, not_38_out, not_39_out, s0, not_40_out, op2, op1, op0);
  and and_12 (and_12_out, not_41_out, not_42_out, not_43_out, s0, op3, not_44_out, not_45_out);
  and and_13 (and_13_out, not_46_out, not_47_out, not_48_out, s0, op3, not_49_out, not_50_out);
  and and_14 (and_14_out, not_51_out, not_52_out, not_53_out, s0, op3, not_54_out, op1, not_55_out);
  and and_15 (and_15_out, not_56_out, not_57_out, not_58_out, s0, not_59_out, not_60_out);
  and and_16 (and_16_out, not_61_out, not_62_out, not_63_out, s0, not_64_out, op2, not_65_out);
  and and_17 (and_17_out, not_66_out, not_67_out, s1, not_68_out, not_69_out, not_70_out);
  and and_18 (and_18_out, not_71_out, not_72_out, not_73_out, s0, op3, not_74_out, not_75_out, op0);
  and and_19 (and_19_out, not_76_out, not_77_out, not_78_out, s0, op3, not_79_out, op1, not_80_out);
  and and_20 (and_20_out, not_81_out, not_82_out, not_83_out, s0, op3, op2, not_84_out, not_85_out);
  and and_21 (and_21_out, not_86_out, not_87_out, not_88_out, s0, not_89_out, op2, op1, not_90_out);
  and and_22 (and_22_out, not_122_out, not_123_out, not_124_out, not_125_out);
  and and_23 (and_23_out, not_91_out, not_92_out, not_93_out, s0, op3, not_94_out, not_95_out, not_96_out);
  and and_24 (and_24_out, not_97_out, not_98_out, not_99_out, s0, op3, not_100_out, op1);
  and and_25 (and_25_out, not_101_out, not_102_out, not_103_out, s0, op3, op2, not_104_out, op0, Z);
  and and_26 (and_26_out, not_105_out, not_106_out, not_107_out, s0, op3, op2, op1, not_108_out, M);
  and and_27 (and_27_out, not_109_out, not_110_out, not_111_out, s0, op3, op2, op1, op0, C);
  and and_28 (and_28_out, not_112_out, not_113_out, s1, not_114_out, not_115_out, not_116_out);
  and and_29 (and_29_out, not_117_out, not_118_out, not_119_out, s0, op3, not_120_out, op1, op0);
  or or_1 (NS3, and_1_out, and_2_out, and_3_out, and_4_out, and_5_out, and_6_out, and_7_out, and_8_out);
  or or_2 (NS2, and_9_out, and_10_out, and_11_out, and_12_out, and_13_out, and_14_out);
  or or_3 (NS1, and_15_out, and_16_out, and_17_out, and_18_out, and_19_out, and_20_out, and_21_out);
  or or_4 (NS0, and_22_out, and_23_out, and_24_out, and_25_out, and_26_out, and_27_out, and_28_out, and_29_out);
endmodule

module test_LDA (
  input  in_1,
  input  in_2,
  input  in_3
);

  wire decoder_1_out0, decoder_1_out1, decoder_1_out2, decoder_1_out3, decoder_1_out4, decoder_1_out6;
  wire [1:0] not_1_out;
  wire [3:0] control_unit_1_state, controlled_buffer_1_out, controlled_buffer_1_out_3,
       controlled_buffer_1_out_4, multiplexer_4_out, PC_q, PC_q_3, split_nibble_1_full_output,
       split_nibble_1_full_output_2, split_nibble_1_full_output_3, split_nibble_1_full_output_4,
       split_nibble_1_nibble;
  wire [7:4] controlled_buffer_1_out_2, PC_q_2;
  wire [11:0] bit_extender_1_out;
  wire [15:0] Accumulator_q, alu_1_output, bit_extender_2_out, Data_Reg_q, IR_q, multiplexer_1_out,
       multiplexer_2_out, multiplexer_3_out, ram_1_data;

  Bit_Extender #(.in_width(16), .out_width(12)) bit_extender_1 (.in(alu_1_output), .out(bit_extender_1_out));
  Register #(.width(12), .trigger("falling")) PC (
    .D(bit_extender_1_out), .en(1'b1), .Q({PC_q_3, PC_q_2, PC_q}), .clk(decoder_1_out0));  // open: clr
  Control__Unit control_unit_1 (
    .opcode(split_nibble_1_nibble), .Z(in_1), .M(in_2), .C(in_3), .state(control_unit_1_state));
  Decoder #(.select(4), .disabled(0), .enable("false")) decoder_1 (
    .out0(decoder_1_out0), .out1(decoder_1_out1), .out2(decoder_1_out2), .out3(decoder_1_out3),
    .out4(decoder_1_out4), .out5(not_1_out[1]), .out6(decoder_1_out6), .sel(control_unit_1_state));  // open: out7, out8, out9, out10, out11, out12, out13, out14, out15
  Hex_Digit_Display hex_digit_display_1 (.value(PC_q_3));  // open: dp
  assign bit_extender_2_out = {{4{1'b0}}, {PC_q_3, PC_q_2, PC_q}};  // Bit_Extender bit_extender_2
  Hex_Digit_Display hex_digit_display_2 (.value(PC_q));  // open: dp
  Hex_Digit_Display hex_digit_display_3 (.value(PC_q_2));  // open: dp
  Hex_Digit_Display hex_digit_display_4 (.value(controlled_buffer_1_out_4));  // open: dp
  Hex_Digit_Display hex_digit_display_5 (.value(controlled_buffer_1_out_3));  // open: dp
  Hex_Digit_Display hex_digit_display_6 (.value(controlled_buffer_1_out_2));  // open: dp
  Hex_Digit_Display hex_digit_display_7 (.value(controlled_buffer_1_out));  // open: dp
  RAM #(.addrWidth(12), .dataWidth(16)) ram_1 (
    .addr({PC_q_3, PC_q_2, PC_q}), .data(ram_1_data), .sel(1'b1), .clk(decoder_1_out0), .ld(decoder_1_out0));  // open: clr
  Hex_Digit_Display hex_digit_display_8 (.value(split_nibble_1_full_output_4));  // open: dp
  assign {controlled_buffer_1_out_4, controlled_buffer_1_out_3, controlled_buffer_1_out_2, controlled_buffer_1_out} = decoder_1_out0 ? ram_1_data : 16'bz;  // Controlled_Buffer controlled_buffer_1
  Hex_Digit_Display hex_digit_display_9 (.value(split_nibble_1_full_output_3));  // open: dp
  Hex_Digit_Display hex_digit_display_10 (.value(split_nibble_1_full_output_2));  // open: dp
  Register #(.width(16), .trigger("high")) IR (
    .D({controlled_buffer_1_out_4, controlled_buffer_1_out_3, controlled_buffer_1_out_2, controlled_buffer_1_out}),
    .en(1'b1), .Q(IR_q), .clk(decoder_1_out0));  // open: clr
  Register #(.width(16), .trigger("high")) Data_Reg (
    .D({controlled_buffer_1_out_4, controlled_buffer_1_out_3, controlled_buffer_1_out_2, controlled_buffer_1_out}),
    .en(1'b1), .Q(Data_Reg_q), .clk(decoder_1_out0));  // open: clr
  Hex_Digit_Display hex_digit_display_11 (.value(split_nibble_1_nibble));  // open: dp
  Hex_Digit_Display hex_digit_display_12 (.value(split_nibble_1_full_output));  // open: dp
  split_nibble split_nibble_1 (
    .\input (IR_q), .nibble(split_nibble_1_nibble),
    .full_output({split_nibble_1_full_output_4, split_nibble_1_full_output_3, split_nibble_1_full_output_2, split_nibble_1_full_output}));
  Hex_Digit_Display hex_digit_display_13 (.value(control_unit_1_state));  // open: dp
  not not_1 (not_1_out[0], not_1_out[1]);
  Hex_Digit_Display hex_digit_display_14 (.value(alu_1_output[15:12]));  // open: dp
  Multiplexer #(.select(2), .width(16), .disabled(0), .enable("false")) multiplexer_1 (
    .in0(alu_1_output),
    .in1({split_nibble_1_full_output_4, split_nibble_1_full_output_3, split_nibble_1_full_output_2, split_nibble_1_full_output}),
    .in2({controlled_buffer_1_out_4, controlled_buffer_1_out_3, controlled_buffer_1_out_2, controlled_buffer_1_out}),
    .out(multiplexer_1_out), .sel(not_1_out));  // open: in3
  Register #(.width(16)) Accumulator (.D(multiplexer_1_out), .Q(Accumulator_q), .clk(not_1_out[1]));  // open: en, clr
  Hex_Digit_Display hex_digit_display_15 (.value(alu_1_output[7:4]));  // open: dp
  Hex_Digit_Display hex_digit_display_16 (.value(alu_1_output[11:8]));  // open: dp
  Hex_Digit_Display hex_digit_display_17 (.value(alu_1_output[3:0]));  // open: dp
  Multiplexer #(.width(16), .disabled(0), .enable("false")) multiplexer_2 (
    .in0(Data_Reg_q), .in1(16'h1), .out(multiplexer_2_out), .sel(decoder_1_out0));
  Multiplexer #(.width(16), .disabled(0), .enable("false")) multiplexer_3 (
    .in0(Accumulator_q), .in1(bit_extender_2_out), .out(multiplexer_3_out), .sel(decoder_1_out0));
  Multiplexer #(.width(4), .enable("false")) multiplexer_4 (
    .in0(split_nibble_1_nibble), .in1(4'b0000), .out(multiplexer_4_out), .sel(decoder_1_out0));
  ALU alu_1 (
    .input_A(multiplexer_2_out), .input_B(multiplexer_3_out), .enable(decoder_1_out0),
    .\output (alu_1_output), .opcode(multiplexer_4_out));  // open: carry_in, Carry_out
endmodule

module test_ADD (
  input  in_1,
  input  in_2,
  input  in_3
);

  wire decoder_1_out0, decoder_1_out1, decoder_1_out2, decoder_1_out3, decoder_1_out4, decoder_1_out6;
  wire [1:0] not_1_out;
  wire [3:0] control_unit_1_state, controlled_buffer_1_out, controlled_buffer_1_out_3,
       controlled_buffer_1_out_4, multiplexer_4_out, PC_q, PC_q_3, split_nibble_1_full_output,
       split_nibble_1_full_output_2, split_nibble_1_full_output_3, split_nibble_1_full_output_4,
       split_nibble_1_nibble;
  wire [7:4] controlled_buffer_1_out_2, PC_q_2;
  wire [11:0] bit_extender_1_out;
  wire [15:0] Accumulator_q, alu_1_output, bit_extender_2_out, Data_Reg_q, IR_q, multiplexer_1_out,
       multiplexer_2_out, multiplexer_3_out, ram_1_data;

  Register #(.width(12), .trigger("falling")) PC (
    .D(bit_extender_1_out), .en(1'b1), .Q({PC_q_3, PC_q_2, PC_q}), .clk(decoder_1_out0));  // open: clr
  Bit_Extender #(.in_width(16), .out_width(12)) bit_extender_1 (.in(alu_1_output), .out(bit_extender_1_out));
  Control__Unit control_unit_1 (
    .opcode(split_nibble_1_nibble), .Z(in_1), .M(in_2), .C(in_3), .state(control_unit_1_state));
  Decoder #(.select(4), .disabled(0), .enable("false")) decoder_1 (
    .out0(decoder_1_out0), .out1(decoder_1_out1), .out2(decoder_1_out2), .out3(decoder_1_out3),
    .out4(decoder_1_out4), .out5(not_1_out[1]), .out6(decoder_1_out6), .sel(control_unit_1_state));  // open: out7, out8, out9, out10, out11, out12, out13, out14, out15
  Hex_Digit_Display hex_digit_display_1 (.value(PC_q_3));  // open: dp
  assign bit_extender_2_out = {{4{1'b0}}, {PC_q_3, PC_q_2, PC_q}};  // Bit_Extender bit_extender_2
  Hex_Digit_Display hex_digit_display_2 (.value(PC_q));  // open: dp
  Hex_Digit_Display hex_digit_display_3 (.value(PC_q_2));  // open: dp
  Hex_Digit_Display hex_digit_display_4 (.value(controlled_buffer_1_out_3));  // open: dp
  Hex_Digit_Display hex_digit_display_5 (.value(controlled_buffer_1_out_4));  // open: dp
  Hex_Digit_Display hex_digit_display_6 (.value(controlled_buffer_1_out_2));  // open: dp
  Hex_Digit_Display hex_digit_display_7 (.value(controlled_buffer_1_out));  // open: dp
  RAM #(.addrWidth(12), .dataWidth(16)) ram_1 (
    .addr({PC_q_3, PC_q_2, PC_q}), .data(ram_1_data), .sel(1'b1), .clk(decoder_1_out0), .ld(decoder_1_out0));  // open: clr
  Hex_Digit_Display hex_digit_display_8 (.value(split_nibble_1_full_output_4));  // open: dp
  assign {controlled_buffer_1_out_4, controlled_buffer_1_out_3, controlled_buffer_1_out_2, controlled_buffer_1_out} = decoder_1_out0 ? ram_1_data : 16'bz;  // Controlled_Buffer controlled_buffer_1
  Hex_Digit_Display hex_digit_display_9 (.value(split_nibble_1_full_output_2));  // open: dp
  Hex_Digit_Display hex_digit_display_10 (.value(split_nibble_1_full_output_3));  // open: dp
  Register #(.width(16), .trigger("high")) IR (
    .D({controlled_buffer_1_out_4, controlled_buffer_1_out_3, controlled_buffer_1_out_2, controlled_buffer_1_out}),
    .en(1'b1), .Q(IR_q), .clk(decoder_1_out0));  // open: clr
  Register #(.width(16), .trigger("high")) Data_Reg (
    .D({controlled_buffer_1_out_4, controlled_buffer_1_out_3, controlled_buffer_1_out_2, controlled_buffer_1_out}),
    .en(1'b1), .Q(Data_Reg_q), .clk(decoder_1_out0));  // open: clr
  Hex_Digit_Display hex_digit_display_11 (.value(split_nibble_1_nibble));  // open: dp
  Hex_Digit_Display hex_digit_display_12 (.value(split_nibble_1_full_output));  // open: dp
  split_nibble split_nibble_1 (
    .\input (IR_q), .nibble(split_nibble_1_nibble),
    .full_output({split_nibble_1_full_output_4, split_nibble_1_full_output_3, split_nibble_1_full_output_2, split_nibble_1_full_output}));
  Hex_Digit_Display hex_digit_display_13 (.value(control_unit_1_state));  // open: dp
  not not_1 (not_1_out[0], not_1_out[1]);
  Hex_Digit_Display hex_digit_display_14 (.value(alu_1_output[15:12]));  // open: dp
  Register #(.width(16)) Accumulator (.D(multiplexer_1_out), .Q(Accumulator_q), .clk(not_1_out[1]));  // open: en, clr
  Multiplexer #(.select(2), .width(16), .disabled(0), .enable("false")) multiplexer_1 (
    .in0(alu_1_output),
    .in1({split_nibble_1_full_output_4, split_nibble_1_full_output_3, split_nibble_1_full_output_2, split_nibble_1_full_output}),
    .in2({controlled_buffer_1_out_4, controlled_buffer_1_out_3, controlled_buffer_1_out_2, controlled_buffer_1_out}),
    .out(multiplexer_1_out), .sel(not_1_out));  // open: in3
  Hex_Digit_Display hex_digit_display_15 (.value(alu_1_output[11:8]));  // open: dp
  Hex_Digit_Display hex_digit_display_16 (.value(alu_1_output[7:4]));  // open: dp
  Hex_Digit_Display hex_digit_display_17 (.value(alu_1_output[3:0]));  // open: dp
  Multiplexer #(.width(16), .disabled(0), .enable("false")) multiplexer_2 (
    .in0(Data_Reg_q), .in1(16'h1), .out(multiplexer_2_out), .sel(decoder_1_out0));
  Multiplexer #(.width(16), .disabled(0), .enable("false")) multiplexer_3 (
    .in0(Accumulator_q), .in1(bit_extender_2_out), .out(multiplexer_3_out), .sel(decoder_1_out0));
  Multiplexer #(.width(4), .enable("false")) multiplexer_4 (
    .in0(split_nibble_1_nibble), .in1(4'b0000), .out(multiplexer_4_out), .sel(decoder_1_out0));
  ALU alu_1 (
    .input_A(multiplexer_2_out), .input_B(multiplexer_3_out), .enable(decoder_1_out0),
    .\output (alu_1_output), .opcode(multiplexer_4_out));  // open: carry_in, Carry_out
endmodule
